# Fritzing sketch Circuit diagram of Smart Bin (saved by Fritzing 0.9.3b)
breadboards: 1

parts:
  Part1 = Arduino Uno (Rev3)
  S1 = Momentary Switch [package=ksa_sealed_tac_switch]
  R1 = Resistor [tolerance=±5% resistance=220 package=THT]  # not connected
  LED1 = LED - 5mm [color="Red (633nm)" package="5 mm [THT]"]
  LED2 = LED - 5mm [color="Red (633nm)" package="5 mm [THT]"]
  LED3 = LED - 5mm [color="Red (633nm)" package="5 mm [THT]"]
  J1 = Basic Servo
  hc-sr1 = hc-sr04

nets:
  N1: Part1.D11_PWM/MOSI, LED3.anode
  N2: Part1.D12/MISO, LED2.anode
  N3: Part1.D13/SCK, LED1.anode
  N4: Part1.D5_PWM, hc-sr1.Trig
  N5: Part1.D6_PWM, hc-sr1.Echo
  N6: Part1.D7, J1.pulse
  VCC: Part1.5V, S1.4, J1.vcc, hc-sr1.VCC
  GND: Part1.GND, LED1.cathode, LED2.cathode, LED3.cathode, J1.gnd, hc-sr1.GND
